# Fritzing sketch Circuit (saved by Fritzing 0.5.2b)
breadboards: 1

parts:
  Arduino1 = Arduino
  i2c/SPI_backpack_attached_to_16x2_LCD = LCD screen  # not connected
  Adafruit_DS1307_RTC_board = DS1307 [package=THT]
  TMP36 = Temperature Sensor (Thermistor) [package=THT]

nets:
  N1: Arduino1.+5V, Adafruit_DS1307_RTC_board.SDA_-_I2C_Data, TMP36.pin_0
  N2: Arduino1.GND, TMP36.pin_1
  N3: Arduino1.A4, Adafruit_DS1307_RTC_board.SCL_-_I2C_Clock
  N4: Arduino1.A5, Adafruit_DS1307_RTC_board.SWQ/OUT_-_Clock_Output
